// Logisim project main.circ as structural Verilog: 4 circuits, main circuit main
module main (
  input  [31:0] in_1,
  input  [5:0] x,
  input  [5:0] y,
  input  [31:0] Load_sample,
  input  state,
  input  Load_to_MR1,
  input  Load_to__MR2,
  input  [31:0] in_8,
  input  [31:0] in_9,
  input  [31:0] in_10
);

  wire and_1_out, and_2_out, and_3_out, button_1_out, clk, counter_1_carry, counter_2_carry, mission,
       n32bit_decoder_short_1_dot, n32bit_decoder_short_1_sign, n32bit_decoder_short_2_dot,
       n32bit_decoder_short_2_sign, n32bit_decoder_short_3_dot, n32bit_decoder_short_3_sign,
       n32bit_decoder_short_4_dot, n32bit_decoder_short_4_sign, n32bit_decoder_short_5_dot,
       n32bit_decoder_short_5_sign, n32bit_decoder_short_6_dot, n32bit_decoder_short_6_sign,
       n32bit_decoder_short_7_dot, n32bit_decoder_short_7_sign, n32bit_decoder_short_8_dot,
       n32bit_decoder_short_8_sign, n32bit_decoder_short_9_dot, n32bit_decoder_short_9_sign,
       n32bit_decoder_short_10_dot, n32bit_decoder_short_10_sign, n32bit_decoder_short_11_dot,
       n32bit_decoder_short_11_sign, n32bit_decoder_short_12_dot, n32bit_decoder_short_12_sign, not_1_out,
       not_2_out, reset_2_out, reset_out, s_r_ff_1_q, s_r_ff_3_q, undriven, update_out;
  wire [3:0] adder_1_out, bit_extender_2_out, bit_extender_3_out, matrix_addr_offset, matrix_addr_R1,
       matrix_addr_R2, n32bit_decoder_short_1__0, n32bit_decoder_short_1__1, n32bit_decoder_short_1__1_2,
       n32bit_decoder_short_1__2, n32bit_decoder_short_1__2_2, n32bit_decoder_short_1__3,
       n32bit_decoder_short_1__3_2, n32bit_decoder_short_1__4, n32bit_decoder_short_1__4_2,
       n32bit_decoder_short_1__5, n32bit_decoder_short_2__0, n32bit_decoder_short_2__1,
       n32bit_decoder_short_2__1_2, n32bit_decoder_short_2__2, n32bit_decoder_short_2__2_2,
       n32bit_decoder_short_2__3, n32bit_decoder_short_2__3_2, n32bit_decoder_short_2__4,
       n32bit_decoder_short_2__4_2, n32bit_decoder_short_2__5, n32bit_decoder_short_3__0,
       n32bit_decoder_short_3__1, n32bit_decoder_short_3__1_2, n32bit_decoder_short_3__2,
       n32bit_decoder_short_3__2_2, n32bit_decoder_short_3__3, n32bit_decoder_short_3__3_2,
       n32bit_decoder_short_3__4, n32bit_decoder_short_3__4_2, n32bit_decoder_short_3__5,
       n32bit_decoder_short_4__0, n32bit_decoder_short_4__1, n32bit_decoder_short_4__1_2,
       n32bit_decoder_short_4__2, n32bit_decoder_short_4__2_2, n32bit_decoder_short_4__3,
       n32bit_decoder_short_4__3_2, n32bit_decoder_short_4__4, n32bit_decoder_short_4__4_2,
       n32bit_decoder_short_4__5, n32bit_decoder_short_5__0, n32bit_decoder_short_5__1,
       n32bit_decoder_short_5__1_2, n32bit_decoder_short_5__2, n32bit_decoder_short_5__2_2,
       n32bit_decoder_short_5__3, n32bit_decoder_short_5__3_2, n32bit_decoder_short_5__4,
       n32bit_decoder_short_5__4_2, n32bit_decoder_short_5__5, n32bit_decoder_short_6__0,
       n32bit_decoder_short_6__1, n32bit_decoder_short_6__1_2, n32bit_decoder_short_6__2,
       n32bit_decoder_short_6__2_2, n32bit_decoder_short_6__3, n32bit_decoder_short_6__3_2,
       n32bit_decoder_short_6__4, n32bit_decoder_short_6__4_2, n32bit_decoder_short_6__5,
       n32bit_decoder_short_7__0, n32bit_decoder_short_7__1, n32bit_decoder_short_7__1_2,
       n32bit_decoder_short_7__2, n32bit_decoder_short_7__2_2, n32bit_decoder_short_7__3,
       n32bit_decoder_short_7__3_2, n32bit_decoder_short_7__4, n32bit_decoder_short_7__4_2,
       n32bit_decoder_short_7__5, n32bit_decoder_short_8__0, n32bit_decoder_short_8__1,
       n32bit_decoder_short_8__1_2, n32bit_decoder_short_8__2, n32bit_decoder_short_8__2_2,
       n32bit_decoder_short_8__3, n32bit_decoder_short_8__3_2, n32bit_decoder_short_8__4,
       n32bit_decoder_short_8__4_2, n32bit_decoder_short_8__5, n32bit_decoder_short_9__0,
       n32bit_decoder_short_9__1, n32bit_decoder_short_9__1_2, n32bit_decoder_short_9__2,
       n32bit_decoder_short_9__2_2, n32bit_decoder_short_9__3, n32bit_decoder_short_9__3_2,
       n32bit_decoder_short_9__4, n32bit_decoder_short_9__4_2, n32bit_decoder_short_9__5,
       n32bit_decoder_short_10__0, n32bit_decoder_short_10__1, n32bit_decoder_short_10__1_2,
       n32bit_decoder_short_10__2, n32bit_decoder_short_10__2_2, n32bit_decoder_short_10__3,
       n32bit_decoder_short_10__3_2, n32bit_decoder_short_10__4, n32bit_decoder_short_10__4_2,
       n32bit_decoder_short_10__5, n32bit_decoder_short_11__0, n32bit_decoder_short_11__1,
       n32bit_decoder_short_11__1_2, n32bit_decoder_short_11__2, n32bit_decoder_short_11__2_2,
       n32bit_decoder_short_11__3, n32bit_decoder_short_11__3_2, n32bit_decoder_short_11__4,
       n32bit_decoder_short_11__4_2, n32bit_decoder_short_11__5, n32bit_decoder_short_12__0,
       n32bit_decoder_short_12__1, n32bit_decoder_short_12__1_2, n32bit_decoder_short_12__2,
       n32bit_decoder_short_12__2_2, n32bit_decoder_short_12__3, n32bit_decoder_short_12__3_2,
       n32bit_decoder_short_12__4, n32bit_decoder_short_12__4_2, n32bit_decoder_short_12__5,
       pull_resistor_1_node;
  wire [23:0] bit_extender_1_out;
  wire [31:0] _11, _12, _13, _21, _22, _23, _31, _32, _33, adder_3_out, adder_4_out, addr,
       bit_extender_4_out, dotmatrix_1_p1, dotmatrix_1_p2, f_aspect_ratio, fp_div_2_out, fp_div_3_out,
       fp_mult_3_out, fp_mult_4_out, fp_mult_5_out, h_2, matrix_mult_4x4_1_out11, matrix_mult_4x4_1_out12,
       matrix_mult_4x4_1_out13, matrix_mult_4x4_1_out14, matrix_reg_rev_1_out_11, matrix_reg_rev_1_out_12,
       matrix_reg_rev_1_out_13, matrix_reg_rev_1_out_21, matrix_reg_rev_1_out_22, matrix_reg_rev_1_out_23,
       matrix_reg_rev_1_out_31, matrix_reg_rev_1_out_32, matrix_reg_rev_1_out_33, matrix_reg_rev_2_out_11,
       matrix_reg_rev_2_out_12, matrix_reg_rev_2_out_13, matrix_reg_rev_2_out_21, matrix_reg_rev_2_out_22,
       matrix_reg_rev_2_out_23, matrix_reg_rev_2_out_31, matrix_reg_rev_2_out_32, matrix_reg_rev_2_out_33,
       n64x64_display_controller_1_x12, n64x64_display_controller_1_x21, n64x64_display_controller_1_x22,
       n64x64_display_controller_1_y12, n64x64_display_controller_1_y21, n64x64_display_controller_1_y22,
       R1_11, R2_11, rom_1_data, sample_m_addr, subtractor_1_out, undriven_2, undriven_3,
       vec4_to_vec3_1_out1, vec4_to_vec3_1_out2, vec4_to_vec3_1_out3, w_2;

  Clock clock_1 (.out(clk));
  Button button_1 (.out(button_1_out));
  Pull_Resistor pull_resistor_1 (.node(pull_resistor_1_node));
  Transistor #(.\type ("n"), .width(4)) transistor_1 (.in(4'b0101), .out(pull_resistor_1_node), .gate(mission));
  S_R_Flip_Flop s_r_ff_1 (.Q(s_r_ff_1_q), .preset(and_1_out), .reset(mission));  // open: S, clk, R, Qn, en
  and and_1 (and_1_out, not_2_out, not_1_out);
  not not_1 (not_1_out, mission);
  not not_2 (not_2_out, button_1_out);
  Adder #(.width(4)) adder_1 (.a(pull_resistor_1_node), .b(matrix_addr_offset), .out(adder_1_out));  // open: cin, cout
  Bit_Extender #(.in_width(32), .out_width(24)) bit_extender_1 (.in(addr), .out(bit_extender_1_out));
  S_R_Flip_Flop s_r_ff_2 (.Q(mission), .preset(and_2_out), .reset(counter_2_carry));  // open: S, clk, R, Qn, en
  and and_2 (and_2_out, button_1_out, s_r_ff_1_q);
  Multiplier #(.width(32)) multiplier_1 (.a(Load_sample), .b(32'h30), .out(sample_m_addr));  // open: cin, cout
  assign bit_extender_2_out = {{2{1'b0}}, matrix_addr_offset[1:0]};  // Bit_Extender bit_extender_2
  assign bit_extender_3_out = {{2{1'b0}}, matrix_addr_offset[3:2]};  // Bit_Extender bit_extender_3
  Transistor #(.\type ("n"), .width(4)) transistor_2 (.in(adder_1_out), .out(matrix_addr_R1), .gate(Load_to_MR1));
  Transistor #(.\type ("n"), .width(4)) transistor_3 (.in(adder_1_out), .out(matrix_addr_R2), .gate(Load_to__MR2));
  ROM #(.addrWidth(24), .dataWidth(32)) rom_1 (.addr(bit_extender_1_out), .data(rom_1_data));  // open: sel
  S_R_Flip_Flop s_r_ff_3 (
    .S(mission), .clk(clk), .R(counter_2_carry), .Q(s_r_ff_3_q), .reset(counter_2_carry));  // open: Qn, preset, en
  assign bit_extender_4_out = {{24{1'b0}}, {bit_extender_3_out, bit_extender_2_out}};  // Bit_Extender bit_extender_4
  Pull_Resistor pull_resistor_2 (.node(R1_11));
  Transistor #(.\type ("n"), .width(32)) transistor_4 (.in(rom_1_data), .out(R1_11), .gate(Load_to_MR1));
  Pull_Resistor pull_resistor_3 (.node(R2_11));
  Transistor #(.\type ("n"), .width(32)) transistor_5 (.in(rom_1_data), .out(R2_11), .gate(Load_to__MR2));
  Counter #(.width(2), .max('h3)) counter_1 (
    .Q(matrix_addr_offset[3:2]), .carry(counter_1_carry), .clk(and_3_out), .clr(counter_1_carry));  // open: load, D, count
  and and_3 (and_3_out, s_r_ff_3_q, clk);
  Adder #(.width(32)) adder_2 (.a(bit_extender_4_out), .b(sample_m_addr), .out(addr));  // open: cin, cout
  Pull_Resistor pull_resistor_4 (.node(matrix_addr_R1));
  Pull_Resistor pull_resistor_5 (.node(matrix_addr_R2));
  _7_Segment_Display u_7_segment_display_1 (.g(n32bit_decoder_short_1_sign));  // open: f, a, b, e, d, c, dp
  _7_Segment_Display u_7_segment_display_2 (.g(n32bit_decoder_short_2_sign));  // open: f, a, b, e, d, c, dp
  _7_Segment_Display u_7_segment_display_3 (.g(n32bit_decoder_short_3_sign));  // open: f, a, b, e, d, c, dp
  Counter #(.width(2), .max('h3)) counter_2 (
    .Q(matrix_addr_offset[1:0]), .carry(counter_2_carry), .clk(counter_1_carry), .clr(counter_2_carry));  // open: load, D, count
  Hex_Digit_Display hex_digit_display_1 (.value(n32bit_decoder_short_1__4));  // open: dp
  Hex_Digit_Display hex_digit_display_2 (.value(n32bit_decoder_short_1__3));  // open: dp
  Hex_Digit_Display hex_digit_display_3 (.value(n32bit_decoder_short_2__4));  // open: dp
  Hex_Digit_Display hex_digit_display_4 (.value(n32bit_decoder_short_2__3));  // open: dp
  Hex_Digit_Display hex_digit_display_5 (.value(n32bit_decoder_short_3__4));  // open: dp
  Hex_Digit_Display hex_digit_display_6 (.value(n32bit_decoder_short_3__3));  // open: dp
  Button reset (.out(reset_out));
  Hex_Digit_Display hex_digit_display_7 (.value(n32bit_decoder_short_1__2_2));  // open: dp
  Hex_Digit_Display hex_digit_display_8 (.value(n32bit_decoder_short_1__1_2));  // open: dp
  Hex_Digit_Display hex_digit_display_9 (.value(n32bit_decoder_short_2__1_2));  // open: dp
  Hex_Digit_Display hex_digit_display_10 (.value(n32bit_decoder_short_2__2_2));  // open: dp
  Hex_Digit_Display hex_digit_display_11 (.value(n32bit_decoder_short_3__2_2));  // open: dp
  Hex_Digit_Display hex_digit_display_12 (.value(n32bit_decoder_short_3__1_2));  // open: dp
  Hex_Digit_Display hex_digit_display_13 (.value(n32bit_decoder_short_1__0), .dp(n32bit_decoder_short_1_dot));
  Hex_Digit_Display hex_digit_display_14 (.value(n32bit_decoder_short_1__1));  // open: dp
  Hex_Digit_Display hex_digit_display_15 (.value(n32bit_decoder_short_2__0), .dp(n32bit_decoder_short_2_dot));
  Hex_Digit_Display hex_digit_display_16 (.value(n32bit_decoder_short_2__1));  // open: dp
  Hex_Digit_Display hex_digit_display_17 (.value(n32bit_decoder_short_3__1));  // open: dp
  Hex_Digit_Display hex_digit_display_18 (.value(n32bit_decoder_short_3__0), .dp(n32bit_decoder_short_3_dot));
  Hex_Digit_Display hex_digit_display_19 (.value(n32bit_decoder_short_1__2));  // open: dp
  Hex_Digit_Display hex_digit_display_20 (.value(n32bit_decoder_short_1__3_2));  // open: dp
  Hex_Digit_Display hex_digit_display_21 (.value(n32bit_decoder_short_2__3_2));  // open: dp
  Hex_Digit_Display hex_digit_display_22 (.value(n32bit_decoder_short_2__2));  // open: dp
  Hex_Digit_Display hex_digit_display_23 (.value(n32bit_decoder_short_3__2));  // open: dp
  Hex_Digit_Display hex_digit_display_24 (.value(n32bit_decoder_short_3__3_2));  // open: dp
  matrix_reg_rev matrix_reg_rev_1 (
    .in_1(clk), .rst(reset_out), .in_11(R2_11), .in_21(R2_11), .in_31(R2_11), .in_12(R2_11), .in_22(R2_11),
    .in_32(R2_11), .in_13(R2_11), .in_23(R2_11), .in_33(R2_11), ._1__store_by_address_0__store_all(1'b1),
    .val___XXYY_address(matrix_addr_R2), .out_11(matrix_reg_rev_1_out_11), .out_21(matrix_reg_rev_1_out_21),
    .out_31(matrix_reg_rev_1_out_31), .out_12(matrix_reg_rev_1_out_12), .out_22(matrix_reg_rev_1_out_22),
    .out_32(matrix_reg_rev_1_out_32), .out_13(matrix_reg_rev_1_out_13), .out_23(matrix_reg_rev_1_out_23),
    .out_33(matrix_reg_rev_1_out_33));
  matrix_reg_rev matrix_reg_rev_2 (
    .in_1(clk), .rst(reset_out), .in_11(R1_11), .in_21(R1_11), .in_31(R1_11), .in_12(R1_11), .in_22(R1_11),
    .in_32(R1_11), .in_13(R1_11), .in_23(R1_11), .in_33(R1_11), ._1__store_by_address_0__store_all(1'b1),
    .val___XXYY_address(matrix_addr_R1), .out_11(matrix_reg_rev_2_out_11), .out_21(matrix_reg_rev_2_out_21),
    .out_31(matrix_reg_rev_2_out_31), .out_12(matrix_reg_rev_2_out_12), .out_22(matrix_reg_rev_2_out_22),
    .out_32(matrix_reg_rev_2_out_32), .out_13(matrix_reg_rev_2_out_13), .out_23(matrix_reg_rev_2_out_23),
    .out_33(matrix_reg_rev_2_out_33));
  Hex_Digit_Display hex_digit_display_25 (.value(n32bit_decoder_short_1__5));  // open: dp
  Hex_Digit_Display hex_digit_display_26 (.value(n32bit_decoder_short_1__4_2));  // open: dp
  Hex_Digit_Display hex_digit_display_27 (.value(n32bit_decoder_short_2__4_2));  // open: dp
  Hex_Digit_Display hex_digit_display_28 (.value(n32bit_decoder_short_2__5));  // open: dp
  Hex_Digit_Display hex_digit_display_29 (.value(n32bit_decoder_short_3__4_2));  // open: dp
  Hex_Digit_Display hex_digit_display_30 (.value(n32bit_decoder_short_3__5));  // open: dp
  _7_Segment_Display u_7_segment_display_4 (.g(n32bit_decoder_short_4_sign));  // open: f, a, b, e, d, c, dp
  _32bit_decoder_short u_32bit_decoder_short_1 (
    .sign(n32bit_decoder_short_1_sign), ._4(n32bit_decoder_short_1__4), ._3(n32bit_decoder_short_1__3),
    ._2_2(n32bit_decoder_short_1__2_2), ._1_2(n32bit_decoder_short_1__1_2), ._0(n32bit_decoder_short_1__0),
    .dot(n32bit_decoder_short_1_dot), .in(_11), ._1(n32bit_decoder_short_1__1),
    ._2(n32bit_decoder_short_1__2), ._3_2(n32bit_decoder_short_1__3_2), ._4_2(n32bit_decoder_short_1__4_2),
    ._5(n32bit_decoder_short_1__5));
  _7_Segment_Display u_7_segment_display_5 (.g(n32bit_decoder_short_5_sign));  // open: f, a, b, e, d, c, dp
  _32bit_decoder_short u_32bit_decoder_short_2 (
    .sign(n32bit_decoder_short_2_sign), ._4(n32bit_decoder_short_2__4), ._3(n32bit_decoder_short_2__3),
    ._2_2(n32bit_decoder_short_2__2_2), ._1_2(n32bit_decoder_short_2__1_2), ._0(n32bit_decoder_short_2__0),
    .dot(n32bit_decoder_short_2_dot), .in(_12), ._1(n32bit_decoder_short_2__1),
    ._2(n32bit_decoder_short_2__2), ._3_2(n32bit_decoder_short_2__3_2), ._4_2(n32bit_decoder_short_2__4_2),
    ._5(n32bit_decoder_short_2__5));
  _7_Segment_Display u_7_segment_display_6 (.g(n32bit_decoder_short_6_sign));  // open: f, a, b, e, d, c, dp
  _32bit_decoder_short u_32bit_decoder_short_3 (
    .sign(n32bit_decoder_short_3_sign), ._4(n32bit_decoder_short_3__4), ._3(n32bit_decoder_short_3__3),
    ._2_2(n32bit_decoder_short_3__2_2), ._1_2(n32bit_decoder_short_3__1_2), ._0(n32bit_decoder_short_3__0),
    .dot(n32bit_decoder_short_3_dot), .in(_13), ._1(n32bit_decoder_short_3__1),
    ._2(n32bit_decoder_short_3__2), ._3_2(n32bit_decoder_short_3__3_2), ._4_2(n32bit_decoder_short_3__4_2),
    ._5(n32bit_decoder_short_3__5));
  matrix_mult matrix_mult_1 (
    .in_1(matrix_reg_rev_1_out_11), .in_2(matrix_reg_rev_1_out_21), .in_3(matrix_reg_rev_1_out_31),
    .in_4(matrix_reg_rev_1_out_12), .in_5(matrix_reg_rev_1_out_22), .in_6(matrix_reg_rev_1_out_32),
    .in_7(matrix_reg_rev_1_out_13), .in_8(matrix_reg_rev_1_out_23), .in_9(matrix_reg_rev_1_out_33),
    .in_10(matrix_reg_rev_2_out_11), .in_11(matrix_reg_rev_2_out_21), .in_12(matrix_reg_rev_2_out_31),
    .in_13(matrix_reg_rev_2_out_12), .in_14(matrix_reg_rev_2_out_22), .in_15(matrix_reg_rev_2_out_32),
    .in_16(matrix_reg_rev_2_out_13), .in_17(matrix_reg_rev_2_out_23), .in_18(matrix_reg_rev_2_out_33),
    .out11(_11), .out21(_21), .out31(_31), .out12(_12), .out22(_22), .out32(_32), .out13(_13), .out23(_23),
    .out33(_33));
  Hex_Digit_Display hex_digit_display_31 (.value(n32bit_decoder_short_4__4));  // open: dp
  Hex_Digit_Display hex_digit_display_32 (.value(n32bit_decoder_short_5__4));  // open: dp
  Hex_Digit_Display hex_digit_display_33 (.value(n32bit_decoder_short_6__4));  // open: dp
  _7_Segment_Display u_7_segment_display_7 (.g(undriven));  // open: f, a, b, e, d, c, dp
  Hex_Digit_Display hex_digit_display_34 ();  // open: value, dp
  fp_mult fp_mult_1 (.in1(32'h400000), .in2(32'h8000), .out(h_2));
  fp_mult fp_mult_2 (.in1(32'h400000), .in2(32'h8000), .out(w_2));
  fp_div fp_div_1 (.in1(32'h400000), .in2(32'h400000), .out(f_aspect_ratio));
  fp_mult fp_mult_3 (.in1(32'hffff0000), .in2(32'h3e80000), .out(fp_mult_3_out));
  Hex_Digit_Display hex_digit_display_35 (.value(n32bit_decoder_short_4__2_2));  // open: dp
  Hex_Digit_Display hex_digit_display_36 (.value(n32bit_decoder_short_4__3));  // open: dp
  Hex_Digit_Display hex_digit_display_37 (.value(n32bit_decoder_short_5__2_2));  // open: dp
  Hex_Digit_Display hex_digit_display_38 (.value(n32bit_decoder_short_5__3));  // open: dp
  Hex_Digit_Display hex_digit_display_39 (.value(n32bit_decoder_short_6__2_2));  // open: dp
  Hex_Digit_Display hex_digit_display_40 (.value(n32bit_decoder_short_6__3));  // open: dp
  Hex_Digit_Display hex_digit_display_41 ();  // open: value, dp
  Hex_Digit_Display hex_digit_display_42 ();  // open: value, dp
  fp_mult fp_mult_4 (.in1(fp_mult_3_out), .in2(32'h1999), .out(fp_mult_4_out));
  Subtractor #(.width(32)) subtractor_1 (.a(32'h3e80000), .b(32'h1999), .out(subtractor_1_out));  // open: bin, bout
  Hex_Digit_Display hex_digit_display_43 (.value(n32bit_decoder_short_4__1_2));  // open: dp
  Hex_Digit_Display hex_digit_display_44 (.value(n32bit_decoder_short_4__0), .dp(n32bit_decoder_short_4_dot));
  Hex_Digit_Display hex_digit_display_45 (.value(n32bit_decoder_short_5__1_2));  // open: dp
  Hex_Digit_Display hex_digit_display_46 (.value(n32bit_decoder_short_5__0), .dp(n32bit_decoder_short_5_dot));
  Hex_Digit_Display hex_digit_display_47 (.value(n32bit_decoder_short_6__0), .dp(n32bit_decoder_short_6_dot));
  Hex_Digit_Display hex_digit_display_48 (.value(n32bit_decoder_short_6__1_2));  // open: dp
  Hex_Digit_Display hex_digit_display_49 ();  // open: value, dp
  Hex_Digit_Display hex_digit_display_50 ();  // open: value, dp
  fp_mult fp_mult_5 (.in1(f_aspect_ratio), .in2(32'h10000), .out(fp_mult_5_out));
  fp_div fp_div_2 (.in1(32'h3e80000), .in2(subtractor_1_out), .out(fp_div_2_out));
  fp_div fp_div_3 (.in1(fp_mult_4_out), .in2(subtractor_1_out), .out(fp_div_3_out));
  Hex_Digit_Display hex_digit_display_51 (.value(n32bit_decoder_short_4__2));  // open: dp
  Hex_Digit_Display hex_digit_display_52 (.value(n32bit_decoder_short_4__1));  // open: dp
  Hex_Digit_Display hex_digit_display_53 (.value(n32bit_decoder_short_5__1));  // open: dp
  Hex_Digit_Display hex_digit_display_54 (.value(n32bit_decoder_short_5__2));  // open: dp
  Hex_Digit_Display hex_digit_display_55 (.value(n32bit_decoder_short_6__2));  // open: dp
  Hex_Digit_Display hex_digit_display_56 (.value(n32bit_decoder_short_6__1));  // open: dp
  Hex_Digit_Display hex_digit_display_57 ();  // open: value, dp
  Hex_Digit_Display hex_digit_display_58 ();  // open: value, dp
  _7_Segment_Display u_7_segment_display_8 (.g(n32bit_decoder_short_7_sign));  // open: f, a, b, e, d, c, dp
  Hex_Digit_Display hex_digit_display_59 (.value(n32bit_decoder_short_4__3_2));  // open: dp
  Hex_Digit_Display hex_digit_display_60 (.value(n32bit_decoder_short_4__4_2));  // open: dp
  Hex_Digit_Display hex_digit_display_61 (.value(n32bit_decoder_short_5__4_2));  // open: dp
  Hex_Digit_Display hex_digit_display_62 (.value(n32bit_decoder_short_5__3_2));  // open: dp
  Hex_Digit_Display hex_digit_display_63 (.value(n32bit_decoder_short_6__3_2));  // open: dp
  Hex_Digit_Display hex_digit_display_64 (.value(n32bit_decoder_short_6__4_2));  // open: dp
  Hex_Digit_Display hex_digit_display_65 ();  // open: value, dp
  Hex_Digit_Display hex_digit_display_66 ();  // open: value, dp
  Hex_Digit_Display hex_digit_display_67 (.value(n32bit_decoder_short_7__4));  // open: dp
  Hex_Digit_Display hex_digit_display_68 (.value(n32bit_decoder_short_7__3));  // open: dp
  Hex_Digit_Display hex_digit_display_69 (.value(n32bit_decoder_short_4__5));  // open: dp
  _32bit_decoder_short u_32bit_decoder_short_4 (
    .sign(n32bit_decoder_short_4_sign), ._4(n32bit_decoder_short_4__4), ._3(n32bit_decoder_short_4__3),
    ._2_2(n32bit_decoder_short_4__2_2), ._1_2(n32bit_decoder_short_4__1_2), ._0(n32bit_decoder_short_4__0),
    .dot(n32bit_decoder_short_4_dot), .in(_21), ._1(n32bit_decoder_short_4__1),
    ._2(n32bit_decoder_short_4__2), ._3_2(n32bit_decoder_short_4__3_2), ._4_2(n32bit_decoder_short_4__4_2),
    ._5(n32bit_decoder_short_4__5));
  Hex_Digit_Display hex_digit_display_70 (.value(n32bit_decoder_short_5__5));  // open: dp
  _32bit_decoder_short u_32bit_decoder_short_5 (
    .sign(n32bit_decoder_short_5_sign), ._4(n32bit_decoder_short_5__4), ._3(n32bit_decoder_short_5__3),
    ._2_2(n32bit_decoder_short_5__2_2), ._1_2(n32bit_decoder_short_5__1_2), ._0(n32bit_decoder_short_5__0),
    .dot(n32bit_decoder_short_5_dot), .in(_22), ._1(n32bit_decoder_short_5__1),
    ._2(n32bit_decoder_short_5__2), ._3_2(n32bit_decoder_short_5__3_2), ._4_2(n32bit_decoder_short_5__4_2),
    ._5(n32bit_decoder_short_5__5));
  Hex_Digit_Display hex_digit_display_71 (.value(n32bit_decoder_short_6__5));  // open: dp
  _32bit_decoder_short u_32bit_decoder_short_6 (
    .sign(n32bit_decoder_short_6_sign), ._4(n32bit_decoder_short_6__4), ._3(n32bit_decoder_short_6__3),
    ._2_2(n32bit_decoder_short_6__2_2), ._1_2(n32bit_decoder_short_6__1_2), ._0(n32bit_decoder_short_6__0),
    .dot(n32bit_decoder_short_6_dot), .in(_23), ._1(n32bit_decoder_short_6__1),
    ._2(n32bit_decoder_short_6__2), ._3_2(n32bit_decoder_short_6__3_2), ._4_2(n32bit_decoder_short_6__4_2),
    ._5(n32bit_decoder_short_6__5));
  Hex_Digit_Display hex_digit_display_72 ();  // open: value, dp
  Hex_Digit_Display hex_digit_display_73 (.value(n32bit_decoder_short_7__1_2));  // open: dp
  Hex_Digit_Display hex_digit_display_74 (.value(n32bit_decoder_short_7__2_2));  // open: dp
  _7_Segment_Display u_7_segment_display_9 (.g(n32bit_decoder_short_8_sign));  // open: f, a, b, e, d, c, dp
  _7_Segment_Display u_7_segment_display_10 (.g(n32bit_decoder_short_9_sign));  // open: f, a, b, e, d, c, dp
  _7_Segment_Display u_7_segment_display_11 (.g(n32bit_decoder_short_10_sign));  // open: f, a, b, e, d, c, dp
  Hex_Digit_Display hex_digit_display_75 (.value(n32bit_decoder_short_7__0), .dp(n32bit_decoder_short_7_dot));
  Hex_Digit_Display hex_digit_display_76 (.value(n32bit_decoder_short_7__1));  // open: dp
  Hex_Digit_Display hex_digit_display_77 (.value(n32bit_decoder_short_8__3));  // open: dp
  Hex_Digit_Display hex_digit_display_78 (.value(n32bit_decoder_short_8__4));  // open: dp
  Hex_Digit_Display hex_digit_display_79 (.value(n32bit_decoder_short_9__4));  // open: dp
  Hex_Digit_Display hex_digit_display_80 (.value(n32bit_decoder_short_9__3));  // open: dp
  Hex_Digit_Display hex_digit_display_81 (.value(n32bit_decoder_short_10__3));  // open: dp
  Hex_Digit_Display hex_digit_display_82 (.value(n32bit_decoder_short_10__4));  // open: dp
  Hex_Digit_Display hex_digit_display_83 (.value(n32bit_decoder_short_7__3_2));  // open: dp
  Hex_Digit_Display hex_digit_display_84 (.value(n32bit_decoder_short_7__2));  // open: dp
  matrix_mult_4x4 matrix_mult_4x4_1 (
    .in_1(in_8), .in_5(in_9), .in_9(in_10), .in_13(32'h10000), .in_17(fp_mult_5_out), .in_22(32'h10000),
    .in_27(fp_div_2_out), .in_28(fp_div_3_out), .in_31(32'h10000), .out11(matrix_mult_4x4_1_out11),
    .out12(matrix_mult_4x4_1_out12), .out13(matrix_mult_4x4_1_out13), .out14(matrix_mult_4x4_1_out14));  // open: in_2, in_3, in_4, in_6, in_7, in_8, in_10, in_11, in_12, in_14, in_15, in_16, in_18, in_19, in_20, in_21, in_23, in_24, in_25, in_26, in_29, in_30, in_32, out21, out31, out41, out22, out32, out42, out23, out33, out43, out24, out34, out44
  Hex_Digit_Display hex_digit_display_85 (.value(n32bit_decoder_short_8__1_2));  // open: dp
  Hex_Digit_Display hex_digit_display_86 (.value(n32bit_decoder_short_8__2_2));  // open: dp
  Hex_Digit_Display hex_digit_display_87 (.value(n32bit_decoder_short_9__2_2));  // open: dp
  Hex_Digit_Display hex_digit_display_88 (.value(n32bit_decoder_short_9__1_2));  // open: dp
  Hex_Digit_Display hex_digit_display_89 (.value(n32bit_decoder_short_10__1_2));  // open: dp
  Hex_Digit_Display hex_digit_display_90 (.value(n32bit_decoder_short_10__2_2));  // open: dp
  Button update (.out(update_out));
  Button reset_2 (.out(reset_2_out));
  Hex_Digit_Display hex_digit_display_91 (.value(n32bit_decoder_short_7__4_2));  // open: dp
  Hex_Digit_Display hex_digit_display_92 (.value(n32bit_decoder_short_7__5));  // open: dp
  _32bit_decoder_short u_32bit_decoder_short_7 (
    .sign(n32bit_decoder_short_7_sign), ._4(n32bit_decoder_short_7__4), ._3(n32bit_decoder_short_7__3),
    ._2_2(n32bit_decoder_short_7__2_2), ._1_2(n32bit_decoder_short_7__1_2), ._0(n32bit_decoder_short_7__0),
    .dot(n32bit_decoder_short_7_dot), .in(vec4_to_vec3_1_out3), ._1(n32bit_decoder_short_7__1),
    ._2(n32bit_decoder_short_7__2), ._3_2(n32bit_decoder_short_7__3_2), ._4_2(n32bit_decoder_short_7__4_2),
    ._5(n32bit_decoder_short_7__5));
  Hex_Digit_Display hex_digit_display_93 (.value(n32bit_decoder_short_8__1));  // open: dp
  Hex_Digit_Display hex_digit_display_94 (.value(n32bit_decoder_short_8__0), .dp(n32bit_decoder_short_8_dot));
  Hex_Digit_Display hex_digit_display_95 (.value(n32bit_decoder_short_9__0), .dp(n32bit_decoder_short_9_dot));
  Hex_Digit_Display hex_digit_display_96 (.value(n32bit_decoder_short_9__1));  // open: dp
  Hex_Digit_Display hex_digit_display_97 (.value(n32bit_decoder_short_10__1));  // open: dp
  Hex_Digit_Display hex_digit_display_98 (.value(n32bit_decoder_short_10__0), .dp(n32bit_decoder_short_10_dot));
  vec4_to_vec3 vec4_to_vec3_1 (
    .in1(matrix_mult_4x4_1_out11), .in2(matrix_mult_4x4_1_out12), .in3(matrix_mult_4x4_1_out13),
    .in4(matrix_mult_4x4_1_out14), .out1(vec4_to_vec3_1_out1), .out2(vec4_to_vec3_1_out2),
    .out3(vec4_to_vec3_1_out3));
  Hex_Digit_Display hex_digit_display_99 (.value(n32bit_decoder_short_8__2));  // open: dp
  Hex_Digit_Display hex_digit_display_100 (.value(n32bit_decoder_short_8__3_2));  // open: dp
  Hex_Digit_Display hex_digit_display_101 (.value(n32bit_decoder_short_9__3_2));  // open: dp
  Hex_Digit_Display hex_digit_display_102 (.value(n32bit_decoder_short_9__2));  // open: dp
  Hex_Digit_Display hex_digit_display_103 (.value(n32bit_decoder_short_10__2));  // open: dp
  Hex_Digit_Display hex_digit_display_104 (.value(n32bit_decoder_short_10__3_2));  // open: dp
  // DotMatrix #(.inputtype("select"), .matrixcols(32), .matrixrows(32), .persist(128)) dotmatrix_1: pin names not known; wires that end beside it: dotmatrix_1_p1, dotmatrix_1_p2
  _64x64_display_controller u_64x64_display_controller_1 (
    .clk(clk), .x11(dotmatrix_1_p1), .x21(n64x64_display_controller_1_x21),
    .x12(n64x64_display_controller_1_x12), .x22(n64x64_display_controller_1_x22), .y11(dotmatrix_1_p2),
    .y21(n64x64_display_controller_1_y21), .y12(n64x64_display_controller_1_y12),
    .y22(n64x64_display_controller_1_y22), .x(x), .y(y), .clear(reset_2_out), .state(state),
    .update_frame(update_out));
  // DotMatrix #(.inputtype("select"), .matrixcols(32), .matrixrows(32), .persist(128)) dotmatrix_2: pin names not known; wires that end beside it: n64x64_display_controller_1_x12, n64x64_display_controller_1_y12
  _7_Segment_Display u_7_segment_display_12 (.g(n32bit_decoder_short_11_sign));  // open: f, a, b, e, d, c, dp
  Hex_Digit_Display hex_digit_display_105 (.value(n32bit_decoder_short_11__4));  // open: dp
  _7_Segment_Display u_7_segment_display_13 (.g(n32bit_decoder_short_12_sign));  // open: f, a, b, e, d, c, dp
  Hex_Digit_Display hex_digit_display_106 (.value(n32bit_decoder_short_12__4));  // open: dp
  Hex_Digit_Display hex_digit_display_107 (.value(n32bit_decoder_short_8__5));  // open: dp
  Hex_Digit_Display hex_digit_display_108 (.value(n32bit_decoder_short_8__4_2));  // open: dp
  _32bit_decoder_short u_32bit_decoder_short_8 (
    .sign(n32bit_decoder_short_8_sign), ._4(n32bit_decoder_short_8__4), ._3(n32bit_decoder_short_8__3),
    ._2_2(n32bit_decoder_short_8__2_2), ._1_2(n32bit_decoder_short_8__1_2), ._0(n32bit_decoder_short_8__0),
    .dot(n32bit_decoder_short_8_dot), .in(_31), ._1(n32bit_decoder_short_8__1),
    ._2(n32bit_decoder_short_8__2), ._3_2(n32bit_decoder_short_8__3_2), ._4_2(n32bit_decoder_short_8__4_2),
    ._5(n32bit_decoder_short_8__5));
  Hex_Digit_Display hex_digit_display_109 (.value(n32bit_decoder_short_9__4_2));  // open: dp
  Hex_Digit_Display hex_digit_display_110 (.value(n32bit_decoder_short_9__5));  // open: dp
  _32bit_decoder_short u_32bit_decoder_short_9 (
    .sign(n32bit_decoder_short_9_sign), ._4(n32bit_decoder_short_9__4), ._3(n32bit_decoder_short_9__3),
    ._2_2(n32bit_decoder_short_9__2_2), ._1_2(n32bit_decoder_short_9__1_2), ._0(n32bit_decoder_short_9__0),
    .dot(n32bit_decoder_short_9_dot), .in(_32), ._1(n32bit_decoder_short_9__1),
    ._2(n32bit_decoder_short_9__2), ._3_2(n32bit_decoder_short_9__3_2), ._4_2(n32bit_decoder_short_9__4_2),
    ._5(n32bit_decoder_short_9__5));
  Hex_Digit_Display hex_digit_display_111 (.value(n32bit_decoder_short_10__5));  // open: dp
  Hex_Digit_Display hex_digit_display_112 (.value(n32bit_decoder_short_10__4_2));  // open: dp
  _32bit_decoder_short u_32bit_decoder_short_10 (
    .sign(n32bit_decoder_short_10_sign), ._4(n32bit_decoder_short_10__4), ._3(n32bit_decoder_short_10__3),
    ._2_2(n32bit_decoder_short_10__2_2), ._1_2(n32bit_decoder_short_10__1_2),
    ._0(n32bit_decoder_short_10__0), .dot(n32bit_decoder_short_10_dot), .in(_33),
    ._1(n32bit_decoder_short_10__1), ._2(n32bit_decoder_short_10__2), ._3_2(n32bit_decoder_short_10__3_2),
    ._4_2(n32bit_decoder_short_10__4_2), ._5(n32bit_decoder_short_10__5));
  Hex_Digit_Display hex_digit_display_113 (.value(n32bit_decoder_short_11__3));  // open: dp
  Hex_Digit_Display hex_digit_display_114 (.value(n32bit_decoder_short_11__2_2));  // open: dp
  Hex_Digit_Display hex_digit_display_115 (.value(n32bit_decoder_short_12__2_2));  // open: dp
  Hex_Digit_Display hex_digit_display_116 (.value(n32bit_decoder_short_12__3));  // open: dp
  Adder #(.width(32)) adder_3 (.a(32'h10000), .b(undriven_2), .out(adder_3_out));  // open: cin, cout
  Adder #(.width(32)) adder_4 (.a(undriven_3), .b(32'h10000), .out(adder_4_out));  // open: cin, cout
  Hex_Digit_Display hex_digit_display_117 (.value(n32bit_decoder_short_11__0), .dp(n32bit_decoder_short_11_dot));
  Hex_Digit_Display hex_digit_display_118 (.value(n32bit_decoder_short_11__1_2));  // open: dp
  Hex_Digit_Display hex_digit_display_119 (.value(n32bit_decoder_short_12__0), .dp(n32bit_decoder_short_12_dot));
  Hex_Digit_Display hex_digit_display_120 (.value(n32bit_decoder_short_12__1_2));  // open: dp
  fp_mult fp_mult_6 (.in1(w_2), .in2(adder_3_out));  // open: out
  fp_mult fp_mult_7 (.in1(adder_4_out), .in2(h_2));  // open: out
  Hex_Digit_Display hex_digit_display_121 (.value(n32bit_decoder_short_11__1));  // open: dp
  Hex_Digit_Display hex_digit_display_122 (.value(n32bit_decoder_short_11__2));  // open: dp
  Hex_Digit_Display hex_digit_display_123 (.value(n32bit_decoder_short_12__1));  // open: dp
  Hex_Digit_Display hex_digit_display_124 (.value(n32bit_decoder_short_12__2));  // open: dp
  // DotMatrix #(.inputtype("select"), .matrixcols(32), .matrixrows(32), .persist(128)) dotmatrix_3: pin names not known; wires that end beside it: n64x64_display_controller_1_x21, n64x64_display_controller_1_y21
  // DotMatrix #(.inputtype("select"), .matrixcols(32), .matrixrows(32), .persist(128)) dotmatrix_4: pin names not known; wires that end beside it: n64x64_display_controller_1_x22, n64x64_display_controller_1_y22
  Hex_Digit_Display hex_digit_display_125 (.value(n32bit_decoder_short_11__3_2));  // open: dp
  Hex_Digit_Display hex_digit_display_126 (.value(n32bit_decoder_short_11__4_2));  // open: dp
  Hex_Digit_Display hex_digit_display_127 (.value(n32bit_decoder_short_12__4_2));  // open: dp
  Hex_Digit_Display hex_digit_display_128 (.value(n32bit_decoder_short_12__3_2));  // open: dp
  Hex_Digit_Display hex_digit_display_129 (.value(n32bit_decoder_short_11__5));  // open: dp
  _32bit_decoder_short u_32bit_decoder_short_11 (
    .sign(n32bit_decoder_short_11_sign), ._4(n32bit_decoder_short_11__4), ._3(n32bit_decoder_short_11__3),
    ._2_2(n32bit_decoder_short_11__2_2), ._1_2(n32bit_decoder_short_11__1_2),
    ._0(n32bit_decoder_short_11__0), .dot(n32bit_decoder_short_11_dot), .in(vec4_to_vec3_1_out1),
    ._1(n32bit_decoder_short_11__1), ._2(n32bit_decoder_short_11__2), ._3_2(n32bit_decoder_short_11__3_2),
    ._4_2(n32bit_decoder_short_11__4_2), ._5(n32bit_decoder_short_11__5));
  Hex_Digit_Display hex_digit_display_130 (.value(n32bit_decoder_short_12__5));  // open: dp
  _32bit_decoder_short u_32bit_decoder_short_12 (
    .sign(n32bit_decoder_short_12_sign), ._4(n32bit_decoder_short_12__4), ._3(n32bit_decoder_short_12__3),
    ._2_2(n32bit_decoder_short_12__2_2), ._1_2(n32bit_decoder_short_12__1_2),
    ._0(n32bit_decoder_short_12__0), .dot(n32bit_decoder_short_12_dot), .in(vec4_to_vec3_1_out2),
    ._1(n32bit_decoder_short_12__1), ._2(n32bit_decoder_short_12__2), ._3_2(n32bit_decoder_short_12__3_2),
    ._4_2(n32bit_decoder_short_12__4_2), ._5(n32bit_decoder_short_12__5));

  // Other names for the same wires on the sheet: R1_12[31:0] = R1_11; R1_13[31:0] = R1_11; R1_21[31:0] = R1_11;
  //   R1_22[31:0] = R1_11; R1_23[31:0] = R1_11; R1_31[31:0] = R1_11; R1_32[31:0] = R1_11; R1_33[31:0] = R1_11;
  //   R2_12[31:0] = R2_11; R2_13[31:0] = R2_11; R2_21[31:0] = R2_11; R2_22[31:0] = R2_11; R2_23[31:0] = R2_11;
  //   R2_31[31:0] = R2_11; R2_32[31:0] = R2_11; R2_33[31:0] = R2_11

  // Notes on the sheet:
  //   in_10: pull=down
  //   in_8: pull=down
  //   Load_sample: pull=down
  //   in_9: pull=down
  //   detect signal section (async)
  //   sync async sig with clk
  //   contents of rom_1 (hex, n*v repeats v):
  //   10000 10000 10000 13*0 10000 10000 10000 13*0 10000 10000 10000 13*0 10000 16*0 10000 16*0 10000
  //   13*0 1000 15*0 1000 15*0 1000 15*0 11000 11000 11000
  //   matrix couter
endmodule

module fp_to_int (
  input  [31:0] in,
  output [31:0] out
);

  Shifter #(.width(32), .shift("lr")) shifter_1 (.in(in), .\dist (5'b10000), .out(out));

  // Notes on the sheet:
  //   in: pull=down
  //   out: pull=down
endmodule

module _64x64_display_controller (
  input  [5:0] y,
  input  [5:0] x,
  input  state,
  input  clear,
  input  update_frame,
  input  clk,
  output [31:0] x12,
  output [31:0] x22,
  output [31:0] x11,
  output [31:0] x21,
  output [31:0] y12,
  output [31:0] y22,
  output [31:0] y11,
  output [31:0] y21
);

  wire and_1_out, and_2_out, and_3_out, counter_1_carry, counter_2_carry, multiplexer_1_out,
       multiplexer_2_out, multiplexer_3_out, multiplexer_6_out, not_1_out, not_2_out, not_3_out, not_4_out,
       not_5_out, not_6_out, or_1_out, s_r_ff_1_q, s_r_ff_2_q, s_r_ff_3_q;
  wire [5:0] counter_2_q, multiplexer_5_out, register_1_q, register_2_q;
  wire [31:0] decoder_1_out0, decoder_2_out0, multiplexer_7_out, multiplexer_8_out, or_2_out,
       pull_resistor_2_node, ram_1_data, ram_2_data, ram_3_data, ram_4_data;

  not not_1 (not_1_out, update_frame);
  and and_1 (and_1_out, update_frame, s_r_ff_1_q);
  S_R_Flip_Flop s_r_ff_1 (.Q(s_r_ff_1_q), .preset(not_1_out), .reset(s_r_ff_2_q));  // open: S, clk, R, Qn, en
  Register #(.width(6)) register_1 (.D(y), .Q(register_1_q), .clk(clk));  // open: en, clr
  Register #(.width(6)) register_2 (.D(x), .Q(register_2_q), .clk(clk));  // open: en, clr
  S_R_Flip_Flop s_r_ff_2 (.Q(s_r_ff_2_q), .preset(and_1_out), .reset(counter_1_carry));  // open: S, clk, R, Qn, en
  Decoder #(.select(5)) decoder_1 (
    .out0(decoder_1_out0[0]), .out1(decoder_1_out0[1]), .out2(decoder_1_out0[2]), .out3(decoder_1_out0[3]),
    .out4(decoder_1_out0[4]), .out5(decoder_1_out0[5]), .out6(decoder_1_out0[6]), .out7(decoder_1_out0[7]),
    .out8(decoder_1_out0[8]), .out9(decoder_1_out0[9]), .out10(decoder_1_out0[10]),
    .out11(decoder_1_out0[11]), .out12(decoder_1_out0[12]), .out13(decoder_1_out0[13]),
    .out14(decoder_1_out0[14]), .out15(decoder_1_out0[15]), .out16(decoder_1_out0[16]),
    .out17(decoder_1_out0[17]), .out18(decoder_1_out0[18]), .out19(decoder_1_out0[19]),
    .out20(decoder_1_out0[20]), .out21(decoder_1_out0[21]), .out22(decoder_1_out0[22]),
    .out23(decoder_1_out0[23]), .out24(decoder_1_out0[24]), .out25(decoder_1_out0[25]),
    .out26(decoder_1_out0[26]), .out27(decoder_1_out0[27]), .out28(decoder_1_out0[28]),
    .out29(decoder_1_out0[29]), .out30(decoder_1_out0[30]), .out31(decoder_1_out0[31]),
    .sel(register_2_q[4:0]), .en(state));
  and and_2 (and_2_out, s_r_ff_2_q, counter_2_carry);
  Pull_Resistor pull_resistor_1 (.node(decoder_1_out0));
  S_R_Flip_Flop s_r_ff_3 (
    .S(and_2_out), .clk(clk), .R(counter_1_carry), .Q(s_r_ff_3_q));  // open: Qn, preset, reset, en
  Multiplexer multiplexer_1 (.in0(state), .in1(1'b0), .out(multiplexer_1_out), .sel(s_r_ff_3_q));  // open: en
  Counter #(.width(6), .max('h3f)) counter_1 (
    .carry(counter_1_carry), .clk(and_3_out));  // open: load, D, count, Q, clr
  and and_3 (and_3_out, clk, s_r_ff_3_q);
  Pull_Resistor pull_resistor_2 (.node(pull_resistor_2_node));
  not not_2 (not_2_out, register_2_q[5]);
  or or_1 (or_1_out, clear, clear);
  assign or_2_out = pull_resistor_2_node | decoder_1_out0;  // OR_Gate or_2, 32 bits wide
  Multiplexer multiplexer_2 (.in0(register_2_q[5]), .in1(1'b1), .out(multiplexer_2_out), .sel(s_r_ff_3_q));  // open: en
  Multiplexer multiplexer_3 (.in0(not_2_out), .in1(1'b1), .out(multiplexer_3_out), .sel(s_r_ff_3_q));  // open: en
  Multiplexer #(.width(32)) multiplexer_4 (
    .in0(ram_3_data), .in1(ram_1_data), .out(pull_resistor_2_node), .sel(multiplexer_3_out), .en(not_3_out));
  Multiplexer #(.width(6)) multiplexer_5 (
    .in0(register_1_q), .in1(counter_2_q), .out(multiplexer_5_out), .sel(s_r_ff_3_q));  // open: en
  Counter #(.width(6), .max('h3f)) counter_2 (
    .Q(counter_2_q), .carry(counter_2_carry), .clk(clk));  // open: load, D, count, clr
  not not_3 (not_3_out, s_r_ff_3_q);
  Decoder #(.select(5)) decoder_2 (
    .out0(decoder_2_out0[0]), .out1(decoder_2_out0[1]), .out2(decoder_2_out0[2]), .out3(decoder_2_out0[3]),
    .out4(decoder_2_out0[4]), .out5(decoder_2_out0[5]), .out6(decoder_2_out0[6]), .out7(decoder_2_out0[7]),
    .out8(decoder_2_out0[8]), .out9(decoder_2_out0[9]), .out10(decoder_2_out0[10]),
    .out11(decoder_2_out0[11]), .out12(decoder_2_out0[12]), .out13(decoder_2_out0[13]),
    .out14(decoder_2_out0[14]), .out15(decoder_2_out0[15]), .out16(decoder_2_out0[16]),
    .out17(decoder_2_out0[17]), .out18(decoder_2_out0[18]), .out19(decoder_2_out0[19]),
    .out20(decoder_2_out0[20]), .out21(decoder_2_out0[21]), .out22(decoder_2_out0[22]),
    .out23(decoder_2_out0[23]), .out24(decoder_2_out0[24]), .out25(decoder_2_out0[25]),
    .out26(decoder_2_out0[26]), .out27(decoder_2_out0[27]), .out28(decoder_2_out0[28]),
    .out29(decoder_2_out0[29]), .out30(decoder_2_out0[30]), .out31(decoder_2_out0[31]), .sel(counter_2_q[4:0]));  // open: en
  Multiplexer multiplexer_6 (.in0(state), .in1(1'b1), .out(multiplexer_6_out), .sel(s_r_ff_3_q));  // open: en
  not not_4 (not_4_out, s_r_ff_3_q);
  RAM #(.addrWidth(6), .dataWidth(32), .bus("separate")) ram_1 (
    .addr(multiplexer_5_out), .din(or_2_out), .data(ram_1_data), .str(multiplexer_1_out),
    .sel(multiplexer_3_out), .clk(clk), .ld(multiplexer_6_out), .clr(or_1_out));
  RAM #(.addrWidth(6), .dataWidth(32), .bus("separate")) ram_2 (
    .addr(counter_2_q), .din(ram_1_data), .data(ram_2_data), .str(s_r_ff_3_q), .clk(clk), .ld(not_4_out));  // open: sel, clr
  not not_5 (not_5_out, s_r_ff_3_q);
  RAM #(.addrWidth(6), .dataWidth(32), .bus("separate")) ram_3 (
    .addr(multiplexer_5_out), .din(or_2_out), .data(ram_3_data), .str(multiplexer_1_out),
    .sel(multiplexer_2_out), .clk(clk), .ld(multiplexer_6_out), .clr(or_1_out));
  RAM #(.addrWidth(6), .dataWidth(32), .bus("separate")) ram_4 (
    .addr(counter_2_q), .din(ram_3_data), .data(ram_4_data), .str(s_r_ff_3_q), .clk(clk), .ld(not_5_out));  // open: sel, clr
  Multiplexer #(.width(32)) multiplexer_7 (
    .in0(ram_4_data), .in1(ram_3_data), .out(multiplexer_7_out), .sel(s_r_ff_3_q));  // open: en
  Multiplexer #(.width(32)) multiplexer_8 (
    .in0(ram_2_data), .in1(ram_1_data), .out(multiplexer_8_out), .sel(s_r_ff_3_q));  // open: en
  not not_6 (not_6_out, counter_2_q[5]);
  Register #(.width(32)) register_3 (.D(multiplexer_7_out), .en(not_6_out), .Q(x22), .clk(clk), .clr(counter_2_q[5]));
  Register #(.width(32)) register_4 (.D(multiplexer_7_out), .en(counter_2_q[5]), .Q(x21), .clk(clk), .clr(not_6_out));
  Register #(.width(32)) register_5 (.D(decoder_2_out0), .en(not_6_out), .Q(y12), .clk(clk), .clr(counter_2_q[5]));
  Register #(.width(32)) register_6 (.D(decoder_2_out0), .en(counter_2_q[5]), .Q(y11), .clk(clk), .clr(not_6_out));
  Register #(.width(32)) register_7 (.D(multiplexer_8_out), .en(not_6_out), .Q(x12), .clk(clk), .clr(counter_2_q[5]));
  Register #(.width(32)) register_8 (.D(multiplexer_8_out), .en(counter_2_q[5]), .Q(x11), .clk(clk), .clr(not_6_out));
  Register #(.width(32)) register_9 (.D(decoder_2_out0), .en(not_6_out), .Q(y22), .clk(clk), .clr(counter_2_q[5]));
  Register #(.width(32)) register_10 (.D(decoder_2_out0), .en(counter_2_q[5]), .Q(y21), .clk(clk), .clr(not_6_out));

  // Notes on the sheet:
  //   x22: pull=down
  //   x11: pull=down
  //   y11: pull=down
  //   state: pull=down
  //   update_frame: pull=down
  //   y22: pull=down
  //   x: pull=down
  //   y21: pull=down
  //   x12: pull=down
  //   y12: pull=down
  //   clk: pull=down
  //   x21: pull=down
  //   y: pull=down
  //   clear: pull=down
  //   detect sig (async)
  //   sync async sig to mian counter
  //   sync async sig to clk
endmodule

module int_to_fp (
  input  [31:0] in,
  output [31:0] out
);

  Shifter #(.width(32)) shifter_1 (.in(in), .\dist (5'b10000), .out(out));

  // Notes on the sheet:
  //   out: pull=down
  //   in: pull=down
endmodule
